// Digital circuit state_machine_digital.dig as structural Verilog
module state_machine_digital (
  input  in_1,
  input  in_2,
  input  in_3,
  input  in_4,
  input  in_10,
  input  clk,
  input  [1:0] in_16,
  output out_5,
  output out_6,
  output out_7,
  output out_8,
  output out_9,
  output out_11,
  output [5:0] out_12,
  output [5:0] out_13,
  output out_14,
  output [7:0] out_17,
  output [7:0] out_18
);

  wire COM6_p3;

  decoder_5_6 #(.applicationType("GHDL"), .Code_File("C:\\Users\\davol\\embedded_system_design\\digital\\src\\encoder_4_2.vhd")) u_decoder_5_6 (
    .i1(in_1), .i2(in_2), .i3(in_3), .i4(in_4), .pr(in_10), .o1(out_5), .o2(out_6), .o3(out_7), .o4(out_8),
    .mv(out_9), .pr_st(out_11), .err(out_12[5]));
  write_uart_sm #(.applicationType("GHDL"), .Code_File("C:\\Users\\davol\\embedded_system_design\\digital\\src\\write_uart_state_machine.vhd")) u_write_uart_sm (
    .state_vector({out_12[5], out_11, out_9, out_7, out_6, out_5}), .ext_error(out_12[5]), .clk(clk),
    .data_write(out_13), .data_write_bool(out_14));
  // ComPort #(.comPort("COM6")) COM6: pin names not known; wires that end beside it: {in_16, out_13}, out_14, COM6_p3, clk, out_17, COM6_p3

  assign out_12[4:0] = {out_11, out_9, out_7, out_6, out_5};
  assign out_18 = {in_16, out_13};

  // Notes on the sheet:
  //   clk: Hz: 50000
  //   in_16: default 1
endmodule

/* Code of decoder_5_6:
library ieee;
use ieee.std_logic_1164.all;

entity decoder_5_6 is
	port ( i1, i2, i3, i4, pr: in std_logic;
	       o1, o2, o3, o4, mv, pr_st, err: out std_logic);
end entity decoder_5_6;

architecture arc_decoder_5_6 of decoder_5_6 is

begin
    process(i1, i2, i3, i4, pr) is
        variable combined_input: std_logic_vector(4 downto 0);
    begin
        combined_input := pr & i4 & i3 & i2 & i1;
        o1 <= '0';
        o2 <= '0';
        o3 <= '0';
        o4 <= '0';
        mv <= '0';
        pr_st <= '0';
        err <= '0';
        case combined_input is
            when "00001" =>
                o1 <= '1';
            when "00010" =>
                o2 <= '1';
            when "00100" =>
                o3 <= '1';
            when "01000" =>
                o4 <= '1';
            when "00000" =>
                mv <= '1';
            when "10000" =>
                pr_st <= '1';
            when others =>
                err <= '1';
        end case;
    end process;
end arc_decoder_5_6;
*/

/* Code of write_uart_sm:
library ieee;
use ieee.std_logic_1164.all;

entity write_uart_sm is
	port ( state_vector: in std_logic_vector(5 downto 0);
           ext_error: in std_logic;
           clk: in std_logic;
	       data_write: out std_logic_vector(5 downto 0); 
           data_write_bool: out std_logic);
end entity write_uart_sm;

architecture arc_write_uart_sm of write_uart_sm is
    signal state_changed: std_logic;
    signal current_state: std_logic_vector(5 downto 0);
begin
    process(clk) is
    begin
        if (clk = '1' and clk'event) then
            data_write <= state_vector;
            if (state_vector /= current_state and ext_error = '0') then
                state_changed <= '1';
                current_state <= state_vector;
                data_write_bool <= '1';
            else
                data_write_bool <= '0';
            end if;
        end if;
    end process;
end arc_write_uart_sm;
*/
